# Fritzing sketch RemoteUnit (saved by Fritzing 0.9.3b)
breadboards: 1

parts:
  MCU = BluePill
  Receiver = NRF24L01+ Breakout Board

nets:
  N1: MCU.A4, Receiver.CS
  N2: MCU.A5, Receiver.SCK
  N3: MCU.A6, Receiver.MISO
  N4: MCU.A7, Receiver.MOSI
  N5: MCU.B0, Receiver.CE
  N6: MCU.B1, Receiver.IRQ
  3V3: MCU.3V3, Receiver.VCC
  GND: MCU.GND, Receiver.GND

custom parts:
  BluePill: Generic ebay blue pill STM32F103C8 "Blue pill" CPU module. Arm Cortex M3 128KB flash (usually) 20kb ram, RTC on board. Supported by the Arduino IDE for programming. As cheap as an Arduino nano but with more power and memory.
